// Digital circuit lg24.dig as structural Verilog
module lg24 (
  input  T,
  input  Clock,
  output Q,
  output Q_2
);

  wire and_1_out, and_2_out, and_3_out, and_4_out, not_1_out, RS_Latch_nq, RS_Latch_q;

  and and_1 (and_1_out, Q_2, T, Clock);
  and and_2 (and_2_out, Clock, T, Q);
  RS_FF_AS RS_Latch (.S(and_1_out), .R(and_2_out), .Q(RS_Latch_q), .nQ(RS_Latch_nq));
  not not_1 (not_1_out, Clock);
  and and_3 (and_3_out, RS_Latch_q, not_1_out);
  and and_4 (and_4_out, not_1_out, RS_Latch_nq);
  RS_FF_AS RS_Latch_2 (.S(and_3_out), .R(and_4_out), .Q(Q), .nQ(Q_2));
endmodule
