// Digital circuit threephase.dig as structural Verilog
module threephase (
  input  clk,
  input  clk_2,
  input  clk_3,
  input  clk_4,
  input  clk_5,
  input  clk_6,
  output a,
  output b,
  output c,
  output a_2,
  output b_2,
  output c_2,
  output ud,
  output outA,
  output outB,
  output outC
);

  wire d_ff_1_nq, d_ff_1_q, d_ff_2_nq, d_ff_2_q, d_ff_3_nq, d_ff_3_q, d_ff_4_nq, nand_1_out, nand_2_out,
       nand_3_out, nand_4_out, nand_5_out, nand_6_out, nand_7_out, nand_8_out, nand_9_out, nand_10_out,
       nand_11_out, nand_12_out, nor_1_out, nor_2_out, nor_3_out, nor_4_out, nor_5_out, nor_6_out, not_1_out,
       not_2_out, not_3_out, not_4_out, not_5_out, not_6_out, not_7_out, not_8_out, not_9_out, not_10_out,
       not_11_out;

  // ScopeTrigger #(.maxStepCount(100000)) scopetrigger_1: pin names not known; wires that end beside it: clk_2
  not not_1 (not_1_out, clk);
  D_FF d_ff_1 (.D(d_ff_3_nq), .C(not_1_out), .Q(d_ff_1_q), .nQ(d_ff_1_nq));
  D_FF d_ff_2 (.D(d_ff_1_q), .C(not_1_out), .Q(d_ff_2_q), .nQ(d_ff_2_nq));
  D_FF d_ff_3 (.D(d_ff_2_q), .C(not_1_out), .Q(d_ff_3_q), .nQ(d_ff_3_nq));
  D_FF d_ff_4 (.D(d_ff_4_nq), .C(not_1_out), .nQ(d_ff_4_nq));  // open: Q
  nor nor_1 (nor_1_out, d_ff_1_q, d_ff_3_q);
  nor nor_2 (nor_2_out, d_ff_1_q, d_ff_2_nq);
  nor nor_3 (nor_3_out, d_ff_3_q, d_ff_2_nq);
  nor nor_4 (nor_4_out, d_ff_1_nq, d_ff_3_nq);
  nor nor_5 (nor_5_out, d_ff_2_q, d_ff_1_nq);
  nor nor_6 (nor_6_out, d_ff_2_q, d_ff_3_nq);
  xor xor_1 (ud, clk_3, d_ff_4_nq, clk_4);
  nand nand_1 (nand_1_out, ud, nor_6_out);
  nand nand_2 (nand_2_out, ud, nor_4_out);
  nand nand_3 (nand_3_out, ud, nor_5_out);
  nand nand_4 (nand_4_out, ud, nor_3_out);
  nand nand_5 (nand_5_out, ud, nor_1_out);
  nand nand_6 (nand_6_out, ud, nor_2_out);
  not not_2 (not_2_out, ud);
  nand nand_7 (nand_7_out, nor_5_out, not_2_out);
  nand nand_8 (nand_8_out, nor_6_out, not_2_out);
  nand nand_9 (nand_9_out, nor_4_out, not_2_out);
  nand nand_10 (nand_10_out, nor_2_out, not_2_out);
  nand nand_11 (nand_11_out, nor_3_out, not_2_out);
  nand nand_12 (nand_12_out, nor_1_out, not_2_out);
  not not_3 (not_3_out, nor_1_out);
  not not_4 (not_4_out, nor_2_out);
  not not_5 (not_5_out, nor_3_out);
  not not_6 (not_6_out, nor_4_out);
  not not_7 (not_7_out, nor_5_out);
  not not_8 (not_8_out, nor_6_out);
  nand nand_13 (a, nand_1_out, not_3_out, nand_7_out);
  nand nand_14 (b, nand_2_out, not_4_out, nand_8_out);
  nand nand_15 (c, nand_3_out, not_5_out, nand_9_out);
  nand nand_16 (a_2, nand_4_out, not_6_out, nand_10_out);
  nand nand_17 (b_2, nand_5_out, not_7_out, nand_11_out);
  nand nand_18 (c_2, nand_6_out, not_8_out, nand_12_out);
  PFET pfet_1 (.G(not_9_out), .S(1'b1), .D(outA));
  not not_9 (not_9_out, a);
  NFET nfet_1 (.G(a_2), .D(outA), .S(1'b0));
  LightBulb lightbulb_1 (.A(outA), .B(outB));
  PFET pfet_2 (.G(not_10_out), .S(1'b1), .D(outB));
  not not_10 (not_10_out, b);
  NFET nfet_2 (.G(b_2), .D(outB), .S(1'b0));
  LightBulb lightbulb_2 (.A(outB), .B(outC));
  not not_11 (not_11_out, c);
  PFET pfet_3 (.G(not_11_out), .S(1'b1), .D(outC));
  NFET nfet_3 (.G(c_2), .D(outC), .S(1'b0));
  LightBulb lightbulb_3 (.A(outC), .B(outA));

  // Notes on the sheet:
  //   clk: Hz: 2
  //   clk_2: Hz: 132
  //   clk_3: Hz: 11
  //   clk_4: Hz: 12
  //   11
  //   12
  //   21
  //   22
  //   13
  //   23
  //   31
  //   33
  //   14
  //   24
  //   32
  //   34
  //   h1
  //   h2
  //   h3
  //   l1
  //   l2
  //   l3
endmodule
